# Fritzing sketch Neopixel-RPi (saved by Fritzing 0.9.3b)
breadboards: 1

parts:
  Raspberry_Pi_1 = Raspberry Pi 3 [part_number=RPI-3-V1.2]
  Part2 = 24 NeoPixel Ring [part_number=1586]
  Part3 = Logic Level Converter
  V1 = DC Power [voltage=5]

nets:
  N1: Raspberry_Pi_1.3v3, Part3.LV
  GND: Raspberry_Pi_1.GND, Part3.GND
  N2: Raspberry_Pi_1.GIPO18, Part3.TX_LV
  N3: Part2.IN, Part3.TX_HV
  N4: Part2.VDD, Part3.HV, V1.V+

notes:
  5V
  GND
  +
  -
  3.3V
  Power Supply
  V
  G
  DI

custom parts:
  24 NeoPixel Ring: 24 ultra bright smart LED NeoPixels are arranged in a circle with 2.6" (66mm) outer diameter. The rings are 'chainable' - connect the output pin of one to the input pin of another. Use only one microcontroller pin to control as many as you can chain together! Each LED is addressable as the driver chip is inside the LED. Each one has ~18mA constant current drive so the color will be very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
